# Fritzing sketch connector_board (saved by Fritzing 0.9.2b)
circuit board: 7.8cm x 5.8cm
perfboards: 1

parts:
  ADXL_345 = Triple Axis Accelerometer Breakout - ADXL345
  J2 = male pin header, 14 pins [form="♂ (male)"]
  J3 = male pin header, 14 pins [form="♂ (male)"]
  J4 = male pin header, 4 pins [form="♂ (male)"]
  J5 = male pin header, 4 pins [form="♂ (male)"]
  J6 = male pin header, 4 pins [form="♂ (male)"]
  Часть2 = 16-Channel 12-bit PCA9685 PWM/Servo Driver

nets:
  GND: ADXL_345.GND, ADXL_345.SDO, J3.pin12, J4.pin4, J5.pin1, J6.pin4, Часть2.GND, Часть2.OE
  VCC: ADXL_345.VCC, ADXL_345.CS, J2.pin14, J4.pin3, J5.pin2, J6.pin3, Часть2.VCC
  N1: ADXL_345.SDA, J2.pin13, J4.pin2, J5.pin3, J6.pin2, Часть2.SDA
  N2: ADXL_345.SCL, J2.pin12, J4.pin1, J5.pin4, J6.pin1, Часть2.SCL

notes:
  g v da cl

custom parts:
  16-Channel 12-bit PCA9685 PWM/Servo Driver: The Adafruit 16-Channel 12-bit PWM/Servo Driver will drive up to 16 servos over I2C with only 2 pins. The on-board PCA9685 PWM controller will drive all 16 channels simultaneously with no additional processing overhead. What's more, you can chain up to 62 of them to control up to 992 servos - all with the same 2 pins
